// Logisim project 7-6.circ as structural Verilog
module _4X4_Ram (
  input  in_1,
  input  in_2,
  input  in_3,
  input  in_4,
  input  in_5,
  input  in_6,
  input  in_7,
  input  in_8,
  output out_9,
  output out_10,
  output out_11,
  output out_12
);
endmodule

module _8X8_Ram (
  input  [7:0] Input,
  input  a2,
  input  a1,
  input  a0,
  input  sel,
  input  r_w,
  output [7:0] Output
);

  wire and_1_out, and_2_out, n4x4_ram_1_out_9, n4x4_ram_1_out_10, n4x4_ram_1_out_11, n4x4_ram_1_out_12,
       n4x4_ram_2_out_9, n4x4_ram_2_out_10, n4x4_ram_2_out_11, n4x4_ram_2_out_12, n4x4_ram_3_out_9,
       n4x4_ram_3_out_10, n4x4_ram_3_out_11, n4x4_ram_3_out_12, n4x4_ram_4_out_9, n4x4_ram_4_out_10,
       n4x4_ram_4_out_11, n4x4_ram_4_out_12, not_1_out;

  not not_1 (not_1_out, a2);
  and and_1 (and_1_out, sel, not_1_out);
  and and_2 (and_2_out, sel, a2);
  _4X4_Ram u_4x4_ram_1 (
    .in_5(a0), .in_6(a1), .in_7(and_1_out), .in_8(r_w), .out_9(n4x4_ram_1_out_9), .out_10(n4x4_ram_1_out_10),
    .out_11(n4x4_ram_1_out_11), .out_12(n4x4_ram_1_out_12), .in_1(Input[7]), .in_2(Input[6]),
    .in_3(Input[5]), .in_4(Input[4]));
  _4X4_Ram u_4x4_ram_2 (
    .in_5(a0), .in_6(a1), .in_7(and_2_out), .in_8(r_w), .out_9(n4x4_ram_2_out_9), .out_10(n4x4_ram_2_out_10),
    .out_11(n4x4_ram_2_out_11), .out_12(n4x4_ram_2_out_12), .in_1(Input[7]), .in_2(Input[6]),
    .in_3(Input[5]), .in_4(Input[4]));
  or or_1 (Output[7], n4x4_ram_2_out_12, n4x4_ram_1_out_12);
  or or_2 (Output[6], n4x4_ram_2_out_11, n4x4_ram_1_out_11);
  or or_3 (Output[5], n4x4_ram_2_out_10, n4x4_ram_1_out_10);
  or or_4 (Output[4], n4x4_ram_2_out_9, n4x4_ram_1_out_9);
  _4X4_Ram u_4x4_ram_3 (
    .in_5(a0), .in_6(a1), .in_7(and_1_out), .in_8(r_w), .out_9(n4x4_ram_3_out_9), .out_10(n4x4_ram_3_out_10),
    .out_11(n4x4_ram_3_out_11), .out_12(n4x4_ram_3_out_12), .in_1(Input[3]), .in_2(Input[2]),
    .in_3(Input[1]), .in_4(Input[0]));
  _4X4_Ram u_4x4_ram_4 (
    .in_5(a0), .in_6(a1), .in_7(and_2_out), .in_8(r_w), .out_9(n4x4_ram_4_out_9), .out_10(n4x4_ram_4_out_10),
    .out_11(n4x4_ram_4_out_11), .out_12(n4x4_ram_4_out_12), .in_1(Input[3]), .in_2(Input[2]),
    .in_3(Input[1]), .in_4(Input[0]));
  or or_5 (Output[3], n4x4_ram_4_out_12, n4x4_ram_3_out_12);
  or or_6 (Output[2], n4x4_ram_4_out_11, n4x4_ram_3_out_11);
  or or_7 (Output[1], n4x4_ram_4_out_10, n4x4_ram_3_out_10);
  or or_8 (Output[0], n4x4_ram_4_out_9, n4x4_ram_3_out_9);

  // Notes on the sheet:
  //   [7:4]
  //   [3:0]
endmodule

module Memory_Cell (
  input  in_1,
  input  in_2
);

  SR_Latch sr_latch_1 (.Reset(in_2), .Set(in_1));  // open: out_3, out_4
endmodule

module SR_Latch (
  input  Reset,
  input  Set,
  output out_3,
  output out_4
);

  nor nor_1 (out_3, Reset, out_4);
  nor nor_2 (out_4, out_3, Set);
endmodule
